// Logisim project Carro.circ as structural Verilog: 2 circuits, main circuit main
module main (
);

  wire button_1_out, clock_1_out, ctrl_m_1_motor_derecho, ctrl_m_1_motor_izquierdo;

  Clock clock_1 (.out(clock_1_out));
  Button button_1 (.out(button_1_out));
  Ctrl_M ctrl_m_1 (
    .Reloj(clock_1_out), .Sensor(button_1_out), .Motor_Izquierdo(ctrl_m_1_motor_izquierdo),
    .Motor_Derecho(ctrl_m_1_motor_derecho));
  LED led_1 (.in(ctrl_m_1_motor_izquierdo));
  LED led_2 (.in(ctrl_m_1_motor_derecho));
endmodule

module Ctrl_M (
  input  Reloj,
  input  Sensor,
  output Motor_Izquierdo,
  output Motor_Derecho
);

  wire and_1_out, and_2_out, and_3_out, and_4_out, d_ff_1_q, d_ff_1_qn, d_ff_2_q, d_ff_2_qn, not_1_out,
       or_1_out, or_2_out;

  and and_1 (and_1_out, d_ff_1_qn, d_ff_2_q);
  not not_1 (not_1_out, Sensor);
  and and_2 (and_2_out, and_1_out, not_1_out);
  and and_3 (and_3_out, d_ff_1_q, Sensor);
  and and_4 (and_4_out, d_ff_1_q, d_ff_2_qn);
  or or_1 (or_1_out, and_2_out, and_3_out);
  or or_2 (or_2_out, or_1_out, and_4_out);
  D_Flip_Flop d_ff_1 (.D(or_2_out), .clk(Reloj), .Q(d_ff_1_q), .Qn(d_ff_1_qn));  // open: preset, reset
  D_Flip_Flop d_ff_2 (.D(Sensor), .clk(Reloj), .Q(d_ff_2_q), .Qn(d_ff_2_qn));  // open: preset, reset
  or or_3 (Motor_Izquierdo, d_ff_1_qn, d_ff_2_qn);
  or or_4 (Motor_Derecho, d_ff_2_qn, d_ff_1_q);
endmodule
